// Logisim project CLA.circ as structural Verilog: 1 circuit, main circuit main
module main (
  input  [3:0] A,
  input  [3:0] B,
  input  Cin,
  output Cout,
  output [3:0] SUM
);

  wire and_1_out, and_2_out, and_3_out, and_4_out, and_5_out, and_6_out, and_7_out, and_8_out, and_9_out,
       and_10_out, C1_out, C2_out, C3_out, G_2_out, G_3_out, G_4_out, G_out, P_2_out, P_3_out, P_4_out, P_out;

  or or_1 (Cout, G_out, and_1_out, and_2_out, and_3_out, and_4_out);
  and and_1 (and_1_out, P_out, P_2_out, P_3_out, P_4_out, Cin);
  and and_2 (and_2_out, P_out, P_2_out, P_3_out, G_4_out);
  and and_3 (and_3_out, P_out, P_2_out, G_3_out);
  and and_4 (and_4_out, P_out, G_2_out);
  xor P (P_out, A[3], B[3]);
  xor S (SUM[3], P_out, C3_out);
  and G (G_out, A[3], B[3]);
  or C3 (C3_out, G_2_out, and_5_out, and_6_out, and_7_out);
  and and_5 (and_5_out, P_2_out, P_3_out, P_4_out, Cin);
  and and_6 (and_6_out, P_2_out, P_3_out, G_4_out);
  and and_7 (and_7_out, P_2_out, G_3_out);
  xor P_2 (P_2_out, A[2], B[2]);
  and G_2 (G_2_out, A[2], B[2]);
  or C2 (C2_out, G_3_out, and_9_out);
  xor S_2 (SUM[2], P_2_out, C2_out);
  and and_8 (and_8_out, P_3_out, P_4_out, Cin);
  and and_9 (and_9_out, P_3_out, G_4_out);
  xor P_3 (P_3_out, A[1], B[1]);
  and G_3 (G_3_out, A[1], B[1]);
  or C1 (C1_out, G_4_out, and_10_out);
  xor S_3 (SUM[1], P_3_out, C1_out);
  and and_10 (and_10_out, P_4_out, Cin);
  xor P_4 (P_4_out, A[0], B[0]);
  xor S_4 (SUM[0], P_4_out, Cin);
  and G_4 (G_4_out, A[0], B[0]);
endmodule
