// Logisim project CSLA.circ as structural Verilog: 3 circuits, main circuit main
module main (
  input  Cin,
  input  [3:0] A,
  input  [3:0] B,
  output [3:0] SUM,
  output Cout
);

  wire not_1_out, ripple_carry_adder_1_cout, ripple_carry_adder_2_cout;
  wire [3:0] ripple_carry_adder_1_sum, ripple_carry_adder_2_sum;

  Ripple_carry_adder ripple_carry_adder_1 (
    .A(A), .B(B), .Cin(1'b0), .Cout(ripple_carry_adder_1_cout), .SUM(ripple_carry_adder_1_sum));
  Multiplexer #(.enable("false")) multiplexer_1 (
    .in0(ripple_carry_adder_1_cout), .in1(ripple_carry_adder_2_cout), .out(Cout), .sel(Cin));
  not not_1 (not_1_out, 1'b0);
  Ripple_carry_adder ripple_carry_adder_2 (
    .A(A), .B(B), .Cin(not_1_out), .Cout(ripple_carry_adder_2_cout), .SUM(ripple_carry_adder_2_sum));
  Multiplexer #(.width(4), .enable("false")) multiplexer_2 (
    .in0(ripple_carry_adder_1_sum), .in1(ripple_carry_adder_2_sum), .out(SUM), .sel(Cin));
endmodule

// RCA
module Ripple_carry_adder (
  input  Cin,
  input  [3:0] A,
  input  [3:0] B,
  output [3:0] SUM,
  output Cout
);

  wire full_adder_1_carry, full_adder_2_carry, full_adder_3_carry;

  full_adder full_adder_1 (.A(Cin), .B(A[0]), .C(B[0]), .SUM(SUM[0]), .CARRY(full_adder_1_carry));
  full_adder full_adder_2 (.A(full_adder_1_carry), .B(A[1]), .C(B[1]), .SUM(SUM[1]), .CARRY(full_adder_2_carry));
  full_adder full_adder_3 (.A(full_adder_2_carry), .B(A[2]), .C(B[2]), .SUM(SUM[2]), .CARRY(full_adder_3_carry));
  full_adder full_adder_4 (.A(full_adder_3_carry), .B(A[3]), .C(B[3]), .SUM(SUM[3]), .CARRY(Cout));
endmodule

// FA
module full_adder (
  input  A,
  input  B,
  input  C,
  output SUM,
  output CARRY
);

  wire and_1_out, and_2_out, and_3_out, xor_1_out;

  xor xor_1 (xor_1_out, A, B);
  and and_1 (and_1_out, A, B);
  and and_2 (and_2_out, A, C);
  and and_3 (and_3_out, B, C);
  xor xor_2 (SUM, xor_1_out, C);
  or or_1 (CARRY, and_1_out, and_2_out, and_3_out);
endmodule
