// Logisim project full_adder1.circ as structural Verilog: 2 circuits, main circuit main
module main (
  input  Cin,
  input  A,
  input  B,
  output SUM,
  output Cout
);

  wire half_adder_1_cout, half_adder_1_sum, half_adder_2_cout;

  half_adder half_adder_1 (.A(A), .B(B), .SUM(half_adder_1_sum), .Cout(half_adder_1_cout));
  half_adder half_adder_2 (.A(Cin), .B(half_adder_1_sum), .SUM(SUM), .Cout(half_adder_2_cout));
  or or_1 (Cout, half_adder_2_cout, half_adder_1_cout);
endmodule

// HA
module half_adder (
  input  A,
  input  B,
  output SUM,
  output Cout
);

  xor xor_1 (SUM, A, B);
  and and_1 (Cout, A, A);
endmodule
