// Logisim project full_adder2.circ as structural Verilog: 1 circuit, main circuit main
module main (
  input  Cin,
  input  A,
  input  B,
  output SUM,
  output Cout
);

  wire xor_1_out;

  xor xor_1 (xor_1_out, A, B);
  Multiplexer #(.enable("false")) multiplexer_1 (.in0(B), .in1(Cin), .out(Cout), .sel(xor_1_out));
  xor xor_2 (SUM, Cin, xor_1_out);
endmodule
