// Logisim project half_adder.circ as structural Verilog: 1 circuit, main circuit main
module main (
  input  A,
  input  B,
  output SUM,
  output Cout
);

  xor xor_1 (SUM, A, B);
  and and_1 (Cout, A, A);
endmodule
